# Fritzing sketch letrack (saved by Fritzing 1.0.4)

parts:
  IR1 = TSOP312.., 314.. [package=THT]
  LED1 = smd LED [color="Red (633nm)" package="0805 [SMD]"]
  Mod2 = Passive Buzzer
  JP5 = Header 6 [package=molex-1x6-ra]
  LED2 = smd LED [color="Red (633nm)" package="0805 [SMD]"]
  IR2 = TSOP312.., 314.. [package=THT]
  Mod3 = Raspberry Pi Pico

nets:
  N1: IR1.GND, LED1.anode, Mod2.-, LED2.anode, IR2.Data, Mod3.pin_3, Mod3.pin_8, Mod3.pin_18, Mod3.pin_28, Mod3.pin_38, Mod3.pin_42
  N2: IR1.Vs, JP5.4
  N3: IR1.Data, Mod3.pin_14
  N4: LED1.cathode, JP5.2
  N5: Mod2.S, Mod3.pin_15
  N6: JP5.1, Mod3.pin_36
  N7: JP5.5, IR2.Vs
  N8: JP5.6, LED2.cathode
  N9: IR2.GND, Mod3.pin_16

custom parts:
  Raspberry Pi Pico: Raspberry Pi Pico. Based around the RP2040 microcontroller the Pico is a low cost microcontroller device bringing Raspberry Pi quality, cost, and easy of use to the microcontroller space. Jan 2021, Split part in to two versions: tht (this one) and SMD. This one will drill holes for a .1 in header in pcb to allow plugging in the module as well as providing pads to solder the module to the top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
